# Fritzing sketch shematics (saved by Fritzing 0.9.1b)
breadboards: 1

parts:
  Arduino = Arduino Uno (Rev3)
  T1 = TMP36 Temperature Sensor [package="TO92 [THT]"]

nets:
  N1: Arduino.A0, T1.Vout
  N2: Arduino.5V, T1.+Vs
  GND: Arduino.GND, T1.GND
